# Fritzing sketch controller (saved by Fritzing 0.9.3b)
breadboards: 1

parts:
  Part1 = Arduino Nano (Rev3.0)
  S2 = Round Pushbutton
  S3 = Round Pushbutton
  S4 = Round Pushbutton
  Part2 = Thumb Joystick
  LED1 = LED - 3mm [color="Red (633nm)" package="3 mm [THT]"]
  1K_Ohms_Brown_Black_Red_Gold1 = Resistor [tolerance=±5% resistance=470 package=THT]
  U2 = POT [package=alps_pot]
  U3 = POT [package=alps_pot]
  BAT1 = BC9VPC [package=bc9vpc]
  Part3 = NRF24L01+ Breakout Board
  S5 = Toggle Switch spst [package=THT]

nets:
  N1: Part1.D3, S4.leg0
  N2: Part1.D4, S2.leg0
  N3: Part1.D5, Part2.SEL
  N4: Part1.D6, 1K_Ohms_Brown_Black_Red_Gold1.Pin_1
  N5: Part1.D7, S3.leg0
  N6: Part1.D8, Part3.CE
  N7: Part1.D9, Part3.CS
  N8: Part1.D11/MOSI, Part3.MOSI
  N9: Part1.D12/MISO, Part3.MISO
  N10: Part1.VIN, S5.L1
  N11: Part1.A3, U3.S
  N12: Part1.A2, U2.S
  N13: Part1.A1, Part2.VERT
  N14: Part1.A0, Part2.HORZ
  3V3: Part1.3V3, Part3.VCC
  N15: Part1.D13/SCK, Part3.SCK
  N16: S4.leg1, U2.E
  N17: LED1.cathode, U3.E
  N18: LED1.anode, 1K_Ohms_Brown_Black_Red_Gold1.Pin_0
  N19: BAT1.V+, S5.COM

custom parts:
  Toggle Switch spst: Toggle Switch single pole single throw
