# Fritzing sketch receiver (saved by Fritzing 0.9.3b)
breadboards: 1

parts:
  Part1 = Arduino Nano (Rev3.0)
  Part3 = NRF24L01+ Breakout Board
  L298N1 = L298N DC motor driver
  M1 = DC Motor  # not connected
  M2 = DC Motor  # not connected
  U1 = WS2812 RGB LED strip
  1K_Ohms_Brown_Black_Red_Gold1 = Resistor [tolerance=±5% resistance=470 package=THT]
  U3 = LM2596 step down module
  S2 = Toggle Switch spst [package=THT]

nets:
  GND: Part1.GND, Part3.GND
  N1: Part1.D3, L298N1.ENB
  N2: Part1.D4, L298N1.IN1
  N3: Part1.D5, 1K_Ohms_Brown_Black_Red_Gold1.Pin_0
  N4: Part1.D6, L298N1.IN3
  N5: Part1.D7, L298N1.IN4
  N6: Part1.D8, Part3.CE
  N7: Part1.D9, Part3.CS
  N8: Part1.D10, L298N1.ENA
  N9: Part1.D11/MOSI, Part3.MOSI
  N10: Part1.D12/MISO, Part3.MISO
  3V3: Part1.3V3, Part3.VCC
  N11: Part1.D13/SCK, Part3.SCK
  N12: U1.VCC, U3.OUT+
  N13: U1.DOUT, 1K_Ohms_Brown_Black_Red_Gold1.Pin_1
  N14: U3.IN+, S2.L1
  N15: U3.IN-, U3.OUT-

notes:
  12 Volts Nimh 1800mAH

custom parts:
  L298N DC motor driver: 2x DC motor driver with 78M05 positive voltage regulator (7..35 V) L298N: max 46 V, 2 A Set 5 V Enable jumper to enable 5 V regultor (needed for the L298N) and +5 V output at screw terminal or supply external +5 V at screw terminal Set ENA and/or ENB to +5 V to enable motor permanently or supply ENA and/or ENB with PWM signal IN1 and IN2 set rotation directory for motor A (OUT1/OUT2) IN2 and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
  WS2812 RGB LED strip: WS2812 strip
  LM2596 step down module: LM2596 DC-DC step down power supply module 3 A.
  Toggle Switch spst: Toggle Switch single pole single throw
